# Fritzing sketch skema_fan_automation (saved by Fritzing 0.9.3b)
breadboards: 1

parts:
  Part1 = Arduino Uno (Rev3) - ICSP
  CPU1 = NodeMCU WROOM ESP 32
  A1 = ZS-042 RTC Module
  KF-1 = KF-301 Relay [package=THT]
  DHT1 = DHT11 Humitidy and Temperature Sensor (3 pins)
  F1 = Fan - Ventilador [package=THT]
  J1 = 220v plug
  Part2 = LCD1602-I2C

nets:
  5V: Part1.5V, A1.VCC, KF-1.power, DHT1.Plus
  N1: Part1.D8, KF-1.signal
  N2: Part1.A4/SDA, A1.SDA, Part2.SDA
  N3: Part1.A5/SCL, A1.SCL, Part2.SCL
  N4: Part1.D0/RX, CPU1.pin_29
  N5: Part1.D1/TX, CPU1.pin_28
  N6: Part1.D2, DHT1.Signal
  GND: Part1.GND, CPU1.pin_15, A1.GND, KF-1.ground, DHT1.Gnd
  N7: KF-1.C, F1.GND
  N8: KF-1.NO, J1.pin1
  N9: F1.5V, J1.pin2

custom parts:
  NodeMCU WROOM ESP 32: 30 pol Development Kit
  ZS-042 RTC Module: This is the ZS-042 RTC module which uses the Maxim DS3231 real time clock IC. The module has a battery holder for a LIR2032 or CR2032. The module also includes an Atmel AT24C32 32K EEPROM for storing important information. The module can operate at 3V3 and 5V. (Mar 2019) fix size of breadboard image, add mounting holes in pcb view, add buses)
  KF-301 Relay: KF-301
  DHT11 Humitidy and Temperature Sensor (3 pins): DHT11 Humidity and Temperature Sensor (3 pins).
  Fan - Ventilador: Ventilador de 2 pines, se encuentra comunmente en computadoras de escritorio
  220v plug: Generic 220V AC plug.
  LCD1602-I2C: A standard character display, usually with 2x16 characters. Comes in many colors with LCM1602 IIC attached.
